# Fritzing sketch zbutton-mqtt-demo-sketch (saved by Fritzing 0.9.3b)
breadboards: 1

parts:
  5VDC = Header 2 [package=molex-1x2_lock]
  S1 = Pushbutton [package="[THT]"]
  R1 = Resistor [tolerance=±5% resistance=10k package=THT]
  WeMos_D1_Mini2 = WeMos D1 Mini

nets:
  N1: 5VDC.2, S1.Pin_1, S1.Pin_2
  N2: S1.Pin_3, S1.Pin_4, R1.Pin_1, WeMos_D1_Mini2.D5

notes:
  5V DC
